// Logisim project TallerLogica-Combinatorios.circ as structural Verilog: 9 circuits, main circuit ALU
module sumador_simple (
  input  A,
  input  B,
  output S,
  output Cout
);

  xor xor_1 (S, A, B);
  and and_1 (Cout, A, B);
endmodule

module sumador_completo (
  input  Cin,
  input  a,
  input  b,
  output S,
  output Cout
);

  wire sumador_simple_1_cout, sumador_simple_1_s, sumador_simple_2_cout;

  sumador_simple sumador_simple_1 (.A(a), .B(b), .S(sumador_simple_1_s), .Cout(sumador_simple_1_cout));
  sumador_simple sumador_simple_2 (.A(Cin), .B(sumador_simple_1_s), .S(S), .Cout(sumador_simple_2_cout));
  xor xor_1 (Cout, sumador_simple_2_cout, sumador_simple_1_cout);
endmodule

module sumador_4 (
  input  [3:0] a,
  input  [3:0] b,
  output [3:0] S,
  output Cout
);

  wire sumador_completo_1_cout, sumador_completo_2_cout, sumador_completo_3_cout;

  sumador_completo sumador_completo_1 (.Cin(1'b0), .a(a[0]), .b(b[0]), .S(S[0]), .Cout(sumador_completo_1_cout));
  sumador_completo sumador_completo_2 (
    .Cin(sumador_completo_3_cout), .a(a[2]), .b(b[2]), .S(S[2]), .Cout(sumador_completo_2_cout));
  sumador_completo sumador_completo_3 (
    .Cin(sumador_completo_1_cout), .a(a[1]), .b(b[1]), .S(S[1]), .Cout(sumador_completo_3_cout));
  sumador_completo sumador_completo_4 (.Cin(sumador_completo_2_cout), .a(a[3]), .b(b[3]), .S(S[3]), .Cout(Cout));
endmodule

module comparador_cero (
  input  [3:0] in_1,
  output out_2
);

  wire and_1_out, and_2_out, not_1_out, not_2_out, not_3_out, not_4_out;

  not not_1 (not_1_out, in_1[0]);
  not not_2 (not_2_out, in_1[1]);
  not not_3 (not_3_out, in_1[2]);
  not not_4 (not_4_out, in_1[3]);
  and and_1 (and_1_out, not_1_out, not_2_out);
  and and_2 (and_2_out, not_3_out, not_4_out);
  and and_3 (out_2, and_1_out, and_2_out);
endmodule

module sumador_flags (
  input  [3:0] A,
  input  [3:0] B,
  output V,
  output N,
  output [3:0] S,
  output Z,
  output C
);

  wire and_1_out, and_2_out, and_3_out, not_1_out, not_2_out, xor_1_out;

  and and_1 (and_1_out, B[3], A[3]);
  not not_1 (not_1_out, B[3]);
  not not_2 (not_2_out, A[3]);
  and and_2 (and_2_out, not_1_out, not_2_out);
  xor xor_1 (xor_1_out, and_1_out, N);
  and and_3 (and_3_out, and_2_out, N);
  sumador_4 sumador_4_1 (.a(A), .b(B), .S({N, S[2:0]}), .Cout(C));
  or or_1 (V, xor_1_out, and_3_out);
  comparador_cero comparador_cero_1 (.in_1({N, S[2:0]}), .out_2(Z));

  assign S[3] = N;
endmodule

module incrementador_4 (
  input  [3:0] A,
  output [3:0] out_2
);

  sumador_4 sumador_4_1 (.a(A), .b(4'b0001), .S(out_2));  // open: Cout
endmodule

module inversor_4 (
  input  [3:0] in_1,
  input  in_2,
  output [3:0] out_3
);

  wire [3:0] incrementador_4_1_out_2, not_1_out;

  assign not_1_out = ~in_1;  // NOT_Gate not_1, 4 bits wide
  incrementador_4 incrementador_4_1 (.A(not_1_out), .out_2(incrementador_4_1_out_2));
  Multiplexer #(.width(4)) multiplexer_1 (.in0(in_1), .in1(incrementador_4_1_out_2), .out(out_3), .sel(in_2));
endmodule

module ALU (
  input  [3:0] A,
  input  [3:0] B,
  input  [1:0] OP,
  output V,
  output C,
  output N,
  output [3:0] S,
  output Z
);

  wire not_1_out, sumador_flags_1_c, sumador_flags_1_v, sumador_flags_2_c, sumador_flags_2_v;
  wire [3:0] and_1_out, inversor_4_1_out_3, or_1_out, sumador_flags_1_s, sumador_flags_2_s;

  inversor_4 inversor_4_1 (.in_1(B), .in_2(1'b1), .out_3(inversor_4_1_out_3));
  sumador_flags sumador_flags_1 (
    .A(A), .B(B), .V(sumador_flags_1_v), .S(sumador_flags_1_s), .C(sumador_flags_1_c));  // open: N, Z
  sumador_flags sumador_flags_2 (
    .A(A), .B(inversor_4_1_out_3), .V(sumador_flags_2_v), .S(sumador_flags_2_s), .C(sumador_flags_2_c));  // open: N, Z
  assign and_1_out = A & B;  // AND_Gate and_1, 4 bits wide
  assign or_1_out = A | B;  // OR_Gate or_1, 4 bits wide
  not not_1 (not_1_out, sumador_flags_2_c);
  Multiplexer #(.select(2), .width(4)) multiplexer_1 (
    .in0(sumador_flags_1_s), .in1(sumador_flags_2_s), .in2(and_1_out), .in3(or_1_out), .out({N, S[2:0]}),
    .sel(OP));
  Multiplexer #(.select(2)) multiplexer_2 (
    .in0(sumador_flags_1_v), .in1(sumador_flags_2_v), .in2(1'b0), .in3(1'b0), .out(V), .sel(OP));
  Multiplexer #(.select(2)) multiplexer_3 (
    .in0(sumador_flags_1_c), .in1(not_1_out), .in2(1'b0), .in3(1'b0), .out(C), .sel(OP));
  comparador_cero comparador_cero_1 (.in_1({N, S[2:0]}), .out_2(Z));

  assign S[3] = N;
endmodule

module verificador (
  output [3:0] out_1,
  output [3:0] out_2,
  output [1:0] out_3,
  output halt,
  output N,
  output Z,
  output V,
  output C,
  output [3:0] res
);

  wire clock_1_out;

  Clock clock_1 (.out(clock_1_out));
  Counter #(.max('h3ff), .width(10)) counter_1 (
    .clk(clock_1_out), .carry(halt), .Q({out_3, out_2, out_1}));  // open: clr, load, up, count, D
  ALU alu_1 (.A(out_1), .B(out_2), .OP(out_3), .V(N), .C(Z), .N(V), .S(res), .Z(C));
endmodule
